# Fritzing sketch ARCADEBUTTONS-LED-CONTROL (saved by Fritzing 0.9.3b)
breadboards: 1

parts:
  R3 = Resistor [tolerance=±5% resistance=10k package=THT]  # not connected
  R4 = Resistor [tolerance=±5% resistance=10k package=THT]
  R5 = Resistor [tolerance=±5% resistance=10k package=THT]
  S3 = Pushbutton [package="[SMD]"]
  S4 = Pushbutton [package="[SMD]"]
  S5 = Pushbutton [package="[SMD]"]
  S6 = Pushbutton [package="[SMD]"]
  S7 = Pushbutton [package="[SMD]"]
  S8 = Pushbutton [package="[SMD]"]
  R6 = Resistor [tolerance=±5% resistance=10k package=THT]
  R7 = Resistor [tolerance=±5% resistance=10k package=THT]  # not connected
  R8 = Resistor [tolerance=±5% resistance=10k package=THT]
  R9 = Resistor [tolerance=±5% resistance=10k package=THT]
  Resistors = Resistor [tolerance=±5% resistance=10k package=THT]
  12V_Input = 2.1mm Barrel Jack with Terminal Block
  U1 = NodeMCU V3.0
  LED1 = smd LED [color="Red (633nm)" package="1206 [SMD]"]
  LED2 = smd LED [color="Red (633nm)" package="1206 [SMD]"]
  LED3 = smd LED [color="Red (633nm)" package="1206 [SMD]"]
  LED4 = smd LED [color="Red (633nm)" package="1206 [SMD]"]
  LED5 = smd LED [color="Red (633nm)" package="1206 [SMD]"]
  LED6 = smd LED [color="Red (633nm)" package="1206 [SMD]"]

nets:
  N1: R4.Pin_0, R5.Pin_0, R6.Pin_0, R8.Pin_0, R9.Pin_0, Resistors.Pin_0, 12V_Input.POS
  N2: R4.Pin_1, S3.Pin_3, S3.Pin_4
  N3: R5.Pin_1, S4.Pin_3, S4.Pin_4
  N4: S3.Pin_1, S3.Pin_2, S4.Pin_1, S4.Pin_2, S5.Pin_1, S5.Pin_2, S6.Pin_1, S6.Pin_2, S7.Pin_1, S7.Pin_2, S8.Pin_1, S8.Pin_2, 12V_Input.NEG, LED6.anode
  N5: S5.Pin_3, S5.Pin_4, R6.Pin_1
  N6: S6.Pin_3, S6.Pin_4, R8.Pin_1
  N7: S7.Pin_3, S7.Pin_4, R9.Pin_1
  N8: S8.Pin_3, S8.Pin_4, Resistors.Pin_1
  N9: U1.D7, LED1.cathode
  N10: LED1.anode, LED2.cathode
  N11: LED2.anode, LED3.cathode
  N12: LED3.anode, LED4.cathode
  N13: LED4.anode, LED5.cathode
  N14: LED5.anode, LED6.cathode

custom parts:
  NodeMCU V3.0: ESP8266 based NodeMCU
