# Fritzing sketch WS2812B-LED-MQTT-CONTROL-wiring (saved by Fritzing 0.9.3b)

parts:
  U1 = NodeMCU V3.0
  NEOPIXEL1 = Neopixel Strip -- White (30/m) [part_number=1376]
  5V_Power_Supply = 2.1mm Barrel Jack with Terminal Block

nets:
  N1: U1.D5, NEOPIXEL1.Din
  GND: U1.GND, NEOPIXEL1.GND, 5V_Power_Supply.NEG
  VIN: U1.Vin, NEOPIXEL1.+5V, 5V_Power_Supply.POS

custom parts:
  NodeMCU V3.0: ESP8266 based NodeMCU
  Neopixel Strip -- White (30/m): These NeoPixel strips have 30 digitally-addressable pixel LEDs per meter and are very affordable and are only 12.5 mm wide, 10 mm if you remove the strip from the casing.
